# Fritzing sketch wiring (saved by Fritzing 0.9.3b)

parts:
  Bauteil3 = Arduino Pro Mini (5V)
  R1 = Resistor [tolerance=±5% resistance=330 package="2010 [SMD]"]
  LED2 = LED - 3mm [color="Red (633nm)" package="3 mm [THT]"]
  DS1 = DS18B20 1-Wire Temperature Sensor [part_number=DS18B20]
  R2 = Resistor [tolerance=±5% resistance=4.7k package="2010 [SMD]"]
  S3 = Momentary Switch [package=ksa_sealed_tac_switch]
  DS2 = DS18B20 1-Wire Temperature Sensor [part_number=DS18B20]
  VCC1 = Battery
  JP1 = Header 8 [package=1x08_smd_alt]

nets:
  GND: Bauteil3.GND, LED2.cathode, DS1.GND, S3.3, DS2.GND, VCC1.-, JP1.2
  VDD: Bauteil3.VCC, DS1.VDD, R2.Pin_1, DS2.VDD, VCC1.+, JP1.1
  N1: Bauteil3.SCK, JP1.4
  N2: Bauteil3.MISO, JP1.5
  N3: Bauteil3.MOSI, JP1.3
  N4: Bauteil3.D10, JP1.8
  N5: Bauteil3.D8, S3.1
  N6: Bauteil3.D4, R1.Pin_1
  N7: Bauteil3.D3, DS1.DQ, R2.Pin_0, DS2.DQ
  N8: Bauteil3.D2, JP1.7
  N9: R1.Pin_0, LED2.anode
