# Fritzing sketch wiring2 (saved by Fritzing 0.9.3b)

parts:
  Bauteil3 = Arduino Pro Mini (5V)
  R1 = Resistor [tolerance=±5% resistance=330 package="2010 [SMD]"]
  LED2 = LED - 3mm [color="Red (633nm)" package="3 mm [THT]"]
  S3 = Momentary Switch [package=ksa_sealed_tac_switch]
  R3 = Resistor [tolerance=±5% resistance=470k package="2010 [SMD]"]
  R2 = Resistor [tolerance=±5% resistance=100k package="2010 [SMD]"]
  VCC1 = 4 x AAA Battery Mount
  DS1 = DS18B20 1-Wire Temperature Sensor [part_number=DS18B20]
  R4 = Resistor [tolerance=±5% resistance=4.7k package="2010 [SMD]"]
  U1 = CC1101 [part_number=CC1101]

nets:
  N1: Bauteil3.RAW, R3.Pin_1, VCC1.+
  GND: Bauteil3.GND, LED2.cathode, S3.3, VCC1.-, DS1.GND, U1.2
  VCC: Bauteil3.VCC, DS1.VDD, R4.Pin_1, U1.1
  N2: Bauteil3.A0, R3.Pin_0, R2.Pin_1
  N3: Bauteil3.SCK, U1.4
  N4: Bauteil3.MISO, U1.5
  N5: Bauteil3.MOSI, U1.3
  N6: Bauteil3.D10, U1.8
  N7: Bauteil3.D8, S3.1
  N8: Bauteil3.D5, R2.Pin_0
  N9: Bauteil3.D4, R1.Pin_1
  N10: Bauteil3.D3, DS1.DQ, R4.Pin_0
  N11: Bauteil3.D2, U1.7
  N12: R1.Pin_0, LED2.anode
